# Fritzing sketch circuit (saved by Fritzing 0.9.3b)
circuit board: 8.46667cm x 5.64444cm
breadboards: 1

parts:
  Part1 = Photon
  R1 = Resistor [tolerance=±5% resistance=220 package="2512 [SMD]"]
  R2 = Photocell (LDR) [package=THT]

nets:
  N1: Part1.A5, R1.Pin_1
  N2: Part1.GND, R1.Pin_0
  N3: Part1.3V3, R2.pin_1
